# Fritzing sketch file 31 (saved by Fritzing 0.9.4)

parts:
  Part1 = Arduino Uno (Rev3)
  BAT1 = BC9VPC [package=bc9vpc]
  S1 = H-Bridge with L298N
  M1 = DC Motor

nets:
  N1: Part1.D8, S1.IN2
  N2: Part1.D9_PWM, S1.IN1
  N3: Part1.D10_PWM/SS, S1.ENA
  GND: Part1.GND, BAT1.V-, S1.GND
  N4: BAT1.V+, S1.12V
  N5: S1.M1-01, M1.pin_2
  N6: S1.M1-02, M1.pin_1

custom parts:
  H-Bridge with L298N: h-bridge
