# Fritzing sketch file 32 (saved by Fritzing 0.9.4)
breadboards: 2

parts:
  Part1 = Arduino Uno (Rev3)
  Part2 = Arduino Uno (Rev3)
  U1 = POT [package=pot_alpha_rv16af-20]  # not connected
  U2 = POT [package=pot_alpha_rv16af-20]  # not connected
  LED1 = LED - 5mm [color="Red (633nm)" package="5 mm [THT]"]
  R1 = Resistor [tolerance=±5% resistance=220 package=THT]
  LED2 = LED - 5mm [color="Red (633nm)" package="5 mm [THT]"]
  R2 = Resistor [tolerance=±5% resistance=220 package=THT]

nets:
  N1: Part1.A4/SDA, Part2.A4/SDA
  N2: Part1.A5/SCL, Part2.A5/SCL
  N3: Part1.D9_PWM, R1.Pin_1
  N4: Part1.GND, LED1.cathode
  N5: Part2.D5_PWM, R2.Pin_1
  N6: Part2.GND, LED2.cathode
  N7: LED1.anode, R1.Pin_0
  N8: LED2.anode, R2.Pin_0
