# Fritzing sketch file 33 (saved by Fritzing 0.9.4)

parts:
  Part1 = Arduino Uno (Rev3)
  Mod1 = KY-023 Dual Axis Joystick Module [package="Breakout board"]

nets:
  N1: Part1.A0, Mod1.VRx
  N2: Part1.A1, Mod1.VRy
  N3: Part1.D2, Mod1.SW
  5V: Part1.5V, Mod1.+5V
  GND: Part1.GND, Mod1.GND

custom parts:
  KY-023 Dual Axis Joystick Module: KY-023 Dual-Axis Joystick Module.
