# Fritzing sketch file 34 (saved by Fritzing 0.9.4)
breadboards: 1

parts:
  Part1 = Arduino Uno (Rev3)
  Mod1 = KY-023 Dual Axis Joystick Module [package="Breakout board"]
  LED1 = LED - 5mm [color="Red (633nm)" package="5 mm [THT]"]

nets:
  N1: Part1.A0, Mod1.VRx
  N2: Part1.A1, Mod1.VRy
  N3: Part1.D2, Mod1.SW
  N4: Part1.D3_PWM, LED1.anode
  5V: Part1.5V, Mod1.+5V
  GND: Part1.GND, Mod1.GND, LED1.cathode

custom parts:
  KY-023 Dual Axis Joystick Module: KY-023 Dual-Axis Joystick Module.
